# Fritzing sketch DuePCB (saved by Fritzing 1.0.7)
circuit board: 13.6106cm x 5.83314cm
breadboards: 1

parts:
  Seatalk = Camdenboss CTB0158-3 [part_number=CTB0158-3 package=THT]
  PC817 = Sharp PC817 [package=THT]
  SN74LS07N = IC, DIP package, 14 pins [chip_label=SN74LS07N]
  Serial = JST-03JQ-BT [part_number=JST-JQ-BT package=THT]
  LM2596 = LM2596 (TO220) [part_number=LM2596 package="TO220 [THT]"]
  fuse = FUSE [package=fuse_5mm]
  0_1mF = Electrolytic Capacitor [capacitance=0.1mF voltage=35V package="100 mil [THT, electrolytic]"]
  Inductor = Inductor [package="400 mil [THT]"]
  1N5822 = Rectifier Diode [part_number=1N5822 package="300 mil [THT]"]
  0_22mF = Electrolytic Capacitor [capacitance=0.22mF voltage=35V package="100 mil [THT, electrolytic]"]
  47k = Resistor [tolerance=±5% power=0.25W resistance=47k package=THT]
  10k = Resistor [tolerance=±5% power=0.25W resistance=10k package=THT]
  10k_2 = Resistor [tolerance=±5% power=0.25W resistance=10k package=THT]
  10k_3 = Resistor [tolerance=±5% power=0.25W resistance=10k package=THT]
  1k = Resistor [tolerance=±5% power=0.25W resistance=1k package=THT]
  diode = Rectifier Diode [part_number=1N4001 package="300 mil [THT]"]
  4_7k = Resistor [tolerance=±5% power=0.25W resistance=4.7k package=THT]
  10k_4 = Resistor [tolerance=±5% power=0.25W resistance=10k package=THT]
  Due = Arduino Due (Rev2b)
  Serial_2 = JST-03JQ-BT [part_number=JST-JQ-BT package=THT]
  GPIO_EXT = double row male pin header, 16 pins [form="♂ (male)"]

nets:
  N1: Seatalk.pin1, fuse.2
  N2: Seatalk.pin2, SN74LS07N.pin2, 4_7k.Pin_1
  N3: Seatalk.pin3, PC817.Pin_2, SN74LS07N.pin7, Serial.pin2, LM2596.Pin_3, LM2596.Pin_5, LM2596.Tab, 0_1mF.-, 1N5822.anode, 0_22mF.-, 10k_2.Pin_0, diode.cathode, 10k_4.Pin_0, Due.GND
  N4: PC817.Pin_1, diode.anode, 4_7k.Pin_0
  N5: PC817.Pin_4, 10k_3.Pin_1, Due.IOREF
  N6: PC817.Pin_3, 10k_4.Pin_1, Due.D19/RX1, Due.D22
  N7: SN74LS07N.pin1, 10k_3.Pin_0, 1k.Pin_0
  N8: SN74LS07N.pin14, Due.5V
  N9: Serial.pin1, Due.D16/TX2
  N10: Serial.pin3, Due.D17/RX2
  N11: LM2596.Pin_1, fuse.1, 0_1mF.+
  N12: LM2596.Pin_2, Inductor.pin_1, 1N5822.cathode
  N13: LM2596.pin_4, 10k.Pin_0, 10k_2.Pin_1
  N14: Inductor.pin_0, 0_22mF.+, 47k.Pin_1, Due.VIN
  N15: 47k.Pin_0, 10k.Pin_1
  N16: 1k.Pin_1, Due.D18/TX1
  N17: Serial_2.pin2, GPIO_EXT.pin2, GPIO_EXT.pin3, GPIO_EXT.pin15, GPIO_EXT.pin16
  N18: Serial_2.pin1, GPIO_EXT.pin9
  N19: Serial_2.pin3, GPIO_EXT.pin8

notes:
  SEATALK1 tx+rx - 3.3v Serial
